# Fritzing sketch PlanetFinder (saved by Fritzing 0.9.3b)
breadboards: 1

parts:
  Raspberry_Pi_1 = Raspberry Pi 3 [part_number=RPI-3-V1.2]
  LCD1 = LCD screen
  R1 = Rotary Potentiometer (Small) [maximum_resistance=100kΩ package=THT]
  S1 = Pushbutton [package="[THT]"]
  S2 = Pushbutton [package="[THT]"]
  S3 = Pushbutton [package="[THT]"]
  MOTOR1 = 28BYJ-48 Stepper Motor
  X1 = X113647 Stepper Driver Board [package=board]
  MOTOR2 = 28BYJ-48 Stepper Motor
  X2 = X113647 Stepper Driver Board [package=board]

nets:
  N1: Raspberry_Pi_1.GIPO4, X2.IN1
  N2: Raspberry_Pi_1.GIPO17, X2.IN2
  N3: Raspberry_Pi_1.GIPO27, X2.IN3
  N4: Raspberry_Pi_1.GIPO22, X2.IN4
  N5: Raspberry_Pi_1.GIPO13, S3.Pin_3, S3.Pin_4
  N6: Raspberry_Pi_1.GIPO19, S2.Pin_3, S2.Pin_4
  N7: Raspberry_Pi_1.GIPO26, S1.Pin_3, S1.Pin_4
  GND: Raspberry_Pi_1.GND, LCD1.VSS, LCD1.R/W, LCD1.LED-, R1.leg2, S1.Pin_1, S1.Pin_2, S2.Pin_1, S2.Pin_2, S3.Pin_1, S3.Pin_2
  N8: Raspberry_Pi_1.GIPO21, X1.IN4
  N9: Raspberry_Pi_1.GIPO20, X1.IN3
  N10: Raspberry_Pi_1.GIPO16, X1.IN2
  N11: Raspberry_Pi_1.GIPO12, X1.IN1
  N12: Raspberry_Pi_1.GIPO7, LCD1.RS
  N13: Raspberry_Pi_1.GIPO8, LCD1.E
  N14: Raspberry_Pi_1.GIPO25, LCD1.DB4
  N15: Raspberry_Pi_1.GIPO24, LCD1.DB5
  N16: Raspberry_Pi_1.GIPO23, LCD1.DB6
  N17: Raspberry_Pi_1.GIPO18, LCD1.DB7
  5V: Raspberry_Pi_1.5V, LCD1.VDD, LCD1.LED+, R1.leg1
  N18: LCD1.V0, R1.wiper
  N19: MOTOR1.RED, X1.RED
  N20: MOTOR1.ORANGE, X1.ORANGE
  N21: MOTOR1.YELLOW, X1.YELLOW
  N22: MOTOR1.PINK, X1.PINK
  N23: MOTOR1.BLUE, X1.BLUE
  N24: MOTOR2.RED, X2.RED
  N25: MOTOR2.ORANGE, X2.ORANGE
  N26: MOTOR2.YELLOW, X2.YELLOW
  N27: MOTOR2.PINK, X2.PINK
  N28: MOTOR2.BLUE, X2.BLUE

custom parts:
  X113647 Stepper Driver Board: A common stepper motor driver board based on ULN2003APG darlington array
